# Fritzing sketch robot  (saved by Fritzing 0.9.3b)
breadboards: 6

parts:
  M3 = Stepper Motor - Bipolar
  DRV_3 = DRV 8825 Stepper Motor Carrier, High Current [part_number="DRV 8825"]
  DRV_4 = DRV 8825 Stepper Motor Carrier, High Current [part_number="DRV 8825"]
  DRV_5 = DRV 8825 Stepper Motor Carrier, High Current [part_number="DRV 8825"]
  J2 = Screw terminal - 2 pins [package=THT]
  Part2 = Arduino Nano (Rev3.0)
  C2 = Electrolytic Capacitor [capacitance=1µF package="100 mil [THT, electrolytic]"]
  M4 = Stepper Motor - Bipolar
  M5 = Stepper Motor - Bipolar
  M6 = Stepper Motor - Bipolar
  M7 = Stepper Motor - Bipolar
  M8 = Stepper Motor - Bipolar
  Part4 = Arduino Nano (Rev3.0)
  DRV_9 = DRV 8825 Stepper Motor Carrier, High Current [part_number="DRV 8825"]
  DRV_10 = DRV 8825 Stepper Motor Carrier, High Current [part_number="DRV 8825"]
  DRV_11 = DRV 8825 Stepper Motor Carrier, High Current [part_number="DRV 8825"]
  J4 = Screw terminal - 2 pins [package=THT]
  C3 = Electrolytic Capacitor [capacitance=1µF package="100 mil [THT, electrolytic]"]
  M9 = Stepper Motor - Bipolar
  M10 = Stepper Motor - Bipolar
  M11 = Stepper Motor - Bipolar
  Part5 = Arduino Nano (Rev3.0)
  DRV_12 = DRV 8825 Stepper Motor Carrier, High Current [part_number="DRV 8825"]
  DRV_13 = DRV 8825 Stepper Motor Carrier, High Current [part_number="DRV 8825"]
  DRV_14 = DRV 8825 Stepper Motor Carrier, High Current [part_number="DRV 8825"]
  J5 = Screw terminal - 2 pins [package=THT]
  C4 = Electrolytic Capacitor [capacitance=1µF package="100 mil [THT, electrolytic]"]
  M12 = Stepper Motor - Bipolar
  M13 = Stepper Motor - Bipolar
  M14 = Stepper Motor - Bipolar
  Part6 = Arduino Nano (Rev3.0)
  DRV_15 = DRV 8825 Stepper Motor Carrier, High Current [part_number="DRV 8825"]
  DRV_16 = DRV 8825 Stepper Motor Carrier, High Current [part_number="DRV 8825"]
  DRV_17 = DRV 8825 Stepper Motor Carrier, High Current [part_number="DRV 8825"]
  J6 = Screw terminal - 2 pins [package=THT]
  C5 = Electrolytic Capacitor [capacitance=1µF package="100 mil [THT, electrolytic]"]
  Raspberry_Pi1 = Raspberry Pi B+  # not connected
  HC-SR04_Sensor_1 = HC-SR04 Ultrasonic Distance Sensor
  HC-SR04_Sensor_2 = HC-SR04 Ultrasonic Distance Sensor
  HC-SR04_Sensor_3 = HC-SR04 Ultrasonic Distance Sensor
  HC-SR04_Sensor_4 = HC-SR04 Ultrasonic Distance Sensor  # not connected
  JP1 = USB_MICROB_PLUG [package=micro-b-th]  # not connected
  JP2 = USB_MICROB_PLUG [package=micro-b-th]  # not connected
  JP3 = USB_MICROB_PLUG [package=micro-b-th]  # not connected
  JP4 = USB_MICROB_PLUG [package=micro-b-th]  # not connected
  X1 = USB Connectors [package=usb-a-h]
  X2 = USB Connectors [package=usb-a-h]
  X3 = USB Connectors [package=usb-a-h]
  X4 = USB Connectors [package=usb-a-h]
  X5 = USB Connectors [package=usb-a-s-nosilk-female]
  X6 = USB Connectors [package=usb-a-s-nosilk-female]
  X7 = USB Connectors [package=usb-a-s-nosilk-female]
  X8 = USB Connectors [package=usb-a-s-nosilk-female]
  X9 = USB Connectors [package=usb-a-s-nosilk]  # not connected
  X10 = USB Connectors [package=usb-a-s-nosilk]  # not connected
  X11 = USB Connectors [package=usb-a-s-nosilk]  # not connected
  X12 = USB Connectors [package=usb-a-s-nosilk]  # not connected
  U1 = ET312 GPS Receiver [package=et312]  # not connected
  Part7 = Arduino Nano (Rev3.0)  # not connected
  Part8 = Arduino GSM Shield
  Part9 = Arduino Uno (Rev3) - ICSP
  U2 = ET312 GPS Receiver [package=et312]  # not connected
  U3 = RFM22 [package=rfm22-xxx-s2]  # not connected
  X13 = USB Connectors [package=usb-a-s-nosilk]  # not connected
  X14 = USB Connectors [package=usb-a-s-nosilk]  # not connected
  JP5 = USB_MICROB_PLUG [package=micro-b-th]  # not connected
  U4 = CMA3000-D01 [package=cma3000]  # not connected
  U5 = ET312 GPS Receiver [package=et312]  # not connected
  U6 = MLX90614 [package=to-39]  # not connected
  U7 = Triple Axis Accelerometer [package=lfcsp-16]  # not connected
  Part10 = Barometric Pressure Sensor - BMP180 Breakout (GY-68)  # not connected
  U8 = GPS-09838 [package=ls20126]  # not connected

nets:
  N1: M3.A, DRV_3.OUT_1B
  N2: M3.C, DRV_3.OUT_1A
  N3: M3.B, DRV_3.OUT_2A
  N4: M3.D, DRV_3.OUT_2B
  N5: DRV_3.RESET, DRV_3.SLEEP, DRV_4.RESET, DRV_4.SLEEP, DRV_5.RESET, DRV_5.SLEEP
  N6: DRV_3.STEP, Part2.D2
  N7: DRV_3.DIRECTION, Part2.D3
  N8: DRV_3.GROUND_ST/_MT, J2.pin1, C2.+
  N9: DRV_3.GROUND_LOG, DRV_4.GROUND_LOG, DRV_5.GROUND_LOG
  N10: DRV_4.STEP, Part2.D5
  N11: DRV_4.DIRECTION, Part2.D4
  N12: DRV_4.OUT_2B, M4.D
  N13: DRV_4.OUT_2A, M4.B
  N14: DRV_4.OUT_1A, M4.C
  N15: DRV_4.OUT_1B, M4.A
  N16: DRV_5.STEP, Part2.D7
  N17: DRV_5.DIRECTION, Part2.D6
  N18: DRV_5.OUT_2B, M5.D
  N19: DRV_5.OUT_2A, M5.B
  N20: DRV_5.OUT_1A, M5.C
  N21: DRV_5.OUT_1B, M5.A
  N22: J2.pin2, C2.-
  N23: M6.A, DRV_11.OUT_1B
  N24: M6.C, DRV_11.OUT_1A
  N25: M6.B, DRV_11.OUT_2A
  N26: M6.D, DRV_11.OUT_2B
  N27: M7.A, DRV_10.OUT_1B
  N28: M7.C, DRV_10.OUT_1A
  N29: M7.B, DRV_10.OUT_2A
  N30: M7.D, DRV_10.OUT_2B
  N31: M8.A, DRV_9.OUT_1B
  N32: M8.C, DRV_9.OUT_1A
  N33: M8.B, DRV_9.OUT_2A
  N34: M8.D, DRV_9.OUT_2B
  N35: Part4.D2, DRV_11.STEP
  N36: Part4.D3, DRV_11.DIRECTION
  N37: Part4.D4, DRV_10.DIRECTION
  N38: Part4.D5, DRV_10.STEP
  N39: Part4.D6, DRV_9.DIRECTION
  N40: Part4.D7, DRV_9.STEP
  N41: DRV_9.RESET, DRV_9.SLEEP, DRV_10.RESET, DRV_10.SLEEP, DRV_11.RESET, DRV_11.SLEEP
  N42: DRV_9.GROUND_LOG, DRV_10.GROUND_LOG, DRV_11.GROUND_LOG
  N43: DRV_11.GROUND_ST/_MT, J4.pin1, C3.+
  N44: J4.pin2, C3.-
  N45: M9.A, DRV_14.OUT_1B
  N46: M9.C, DRV_14.OUT_1A
  N47: M9.B, DRV_14.OUT_2A
  N48: M9.D, DRV_14.OUT_2B
  N49: M10.A, DRV_13.OUT_1B
  N50: M10.C, DRV_13.OUT_1A
  N51: M10.B, DRV_13.OUT_2A
  N52: M10.D, DRV_13.OUT_2B
  N53: M11.A, DRV_12.OUT_1B
  N54: M11.C, DRV_12.OUT_1A
  N55: M11.B, DRV_12.OUT_2A
  N56: M11.D, DRV_12.OUT_2B
  N57: Part5.D2, DRV_14.STEP
  N58: Part5.D3, DRV_14.DIRECTION
  N59: Part5.D4, DRV_13.DIRECTION
  N60: Part5.D5, DRV_13.STEP
  N61: Part5.D6, DRV_12.DIRECTION
  N62: Part5.D7, DRV_12.STEP
  N63: DRV_12.RESET, DRV_12.SLEEP, DRV_13.RESET, DRV_13.SLEEP, DRV_14.RESET, DRV_14.SLEEP
  N64: DRV_12.GROUND_LOG, DRV_13.GROUND_LOG, DRV_14.GROUND_LOG
  N65: DRV_14.GROUND_ST/_MT, J5.pin1, C4.+
  N66: J5.pin2, C4.-
  N67: M12.A, DRV_17.OUT_1B
  N68: M12.C, DRV_17.OUT_1A
  N69: M12.B, DRV_17.OUT_2A
  N70: M12.D, DRV_17.OUT_2B
  N71: M13.A, DRV_15.OUT_1B
  N72: M13.C, DRV_15.OUT_1A
  N73: M13.B, DRV_15.OUT_2A
  N74: M13.D, DRV_15.OUT_2B
  N75: M14.A, DRV_16.OUT_1B
  N76: M14.C, DRV_16.OUT_1A
  N77: M14.B, DRV_16.OUT_2A
  N78: M14.D, DRV_16.OUT_2B
  N79: Part6.D2, DRV_17.STEP
  N80: Part6.D3, DRV_17.DIRECTION
  N81: Part6.D4, DRV_16.DIRECTION
  N82: Part6.D5, DRV_16.STEP
  N83: Part6.D6, DRV_15.DIRECTION
  N84: Part6.D7, DRV_15.STEP
  N85: DRV_15.RESET, DRV_15.SLEEP, DRV_16.RESET, DRV_16.SLEEP, DRV_17.RESET, DRV_17.SLEEP
  N86: DRV_15.GROUND_LOG, DRV_16.GROUND_LOG, DRV_17.GROUND_LOG
  N87: DRV_17.GROUND_ST/_MT, J6.pin1, C5.+
  N88: J6.pin2, C5.-
  VCC: HC-SR04_Sensor_1.VCC, HC-SR04_Sensor_2.VCC, HC-SR04_Sensor_3.VCC
  GND: HC-SR04_Sensor_1.GND, HC-SR04_Sensor_2.GND, HC-SR04_Sensor_3.GND
  N89: X1.D-, X8.D-
  N90: X1.D+, X8.D+
  N91: X1.VBUS, X8.VBUS
  GND_2: X1.GND, X8.GND
  N92: X2.D-, X5.D-
  N93: X2.D+, X5.D+
  N94: X2.VBUS, X5.VBUS
  GND_3: X2.GND, X5.GND
  N95: X3.D-, X7.D-
  N96: X3.D+, X7.D+
  N97: X3.VBUS, X7.VBUS
  GND_4: X3.GND, X7.GND
  N98: X4.D-, X6.D-
  N99: X4.D+, X6.D+
  GND_5: X4.GND, X6.GND
  N100: Part8.A5/SCL, Part9.A5/SCL
  N101: Part8.A4/SDA, Part9.A4/SDA
  N102: Part8.AREF, Part9.AREF
  N103: Part8.AGND, Part9.GND
  N104: Part8.SCK/D13, Part9.D13/SCK
  N105: Part8.MISO/D12, Part9.D12/MISO
  N106: Part8.MOSI/PWM_D11, Part9.D11_PWM/MOSI
  N107: Part8.SS/PWM_D10, Part9.D10_PWM/SS
  N108: Part8.PWM_D9, Part9.D9_PWM
  N109: Part8.D8, Part9.D8
  N110: Part8.N/C, Part9.N/C
  N111: Part8.IOREF, Part9.IOREF
  N112: Part8.RST_ARDUINO, Part9.RESET
  3V3: Part8.3V3, Part9.3V3
  5V: Part8.5V, Part9.5V
  VIN: Part8.VIN, Part9.VIN
  N113: Part8.N/C_D0, Part9.D0/RX
  N114: Part8.N/C_D1, Part9.D1/TX
  N115: Part8.DSM_RX_D2, Part9.D2
  N116: Part8.DSM_TX_D3, Part9.D3_PWM
  N117: Part8.PWM_D4, Part9.D4
  N118: Part8.PWM_D5, Part9.D5_PWM
  N119: Part8.PWM_D6, Part9.D6_PWM
  N120: Part8.RST_MDM/D7, Part9.D7
  N121: Part8.A0, Part9.A0
  N122: Part8.A1, Part9.A1
  N123: Part8.A2, Part9.A2
  N124: Part8.A3, Part9.A3
